# Fritzing sketch AlarmPi LED Strip only (saved by Fritzing 0.9.6b)
circuit board: 6.5cm x 5.53cm
breadboards: 1

parts:
  Raspberry_P1 = double row female pin header, 40 pins [form="♀ (female)"]
  Button_1 = male pin header, 2 pins [form="♂ (male)"]
  Button_2 = male pin header, 2 pins [form="♂ (male)"]
  220nF = Ceramic Capacitor [capacitance=220nF voltage=35V package="100 mil [THT, multilayer]"]
  IRF3708 = MOSFET-NCHANNEL [part_number=IRF3708 package=to220v]
  220nF_2 = Ceramic Capacitor [capacitance=220nF voltage=35V package="100 mil [THT, multilayer]"]
  470k = Resistor [tolerance=±5% resistance=470k power=0.25 package=THT]
  SPI = male pin header, 4 pins [form="♂ (male)"]
  in = screw terminal, 2 pins
  LED = screw terminal, 2 pins
  +5V = female pin header, 1 pin [form="♀ (female)"]
  GND = female pin header, 1 pin [form="♀ (female)"]
  J20 = female pin header, 1 pin [form="♀ (female)"]  # not connected
  J21 = female pin header, 1 pin [form="♀ (female)"]  # not connected

nets:
  N1: Raspberry_P1.pin1, Raspberry_P1.pin2, SPI.pin4, in.pin2, LED.pin2, +5V.pin1
  N2: Raspberry_P1.pin3, Raspberry_P1.pin10, Raspberry_P1.pin15, Raspberry_P1.pin17, Raspberry_P1.pin21, Raspberry_P1.pin28, Raspberry_P1.pin36, Button_1.pin2, Button_2.pin2, 220nF.1, IRF3708.S, 220nF_2.1, 470k.Pin_1, SPI.pin1, in.pin1, LED.pin1
  N3: Raspberry_P1.pin8, IRF3708.G, 470k.Pin_0
  N4: Raspberry_P1.pin9, Button_2.pin1, 220nF_2.0
  N5: Raspberry_P1.pin11, Button_1.pin1, 220nF.0
  N6: Raspberry_P1.pin29, SPI.pin3
  N7: Raspberry_P1.pin31, SPI.pin2
  N8: IRF3708.D, GND.pin1

notes:
  AlarmPi
  LED1 driver
  LED0 driver
  USB 5V out sound
  Raspberry
  gpio23
  GND
  gpio24
  gpio25
  gpio16
  3,3V
  IIC SDA
  IIC SCL
  SPI MOSI
  SPI SCLK
  Alarm Pi
  +5V
  speaker
  DO
  CLK
  5V
