# Fritzing sketch AlarmPi (saved by Fritzing 0.9.4)
circuit board: 10.3cm x 6.37cm
breadboards: 1

parts:
  Raspberry_P1 = double row female pin header, 40 pins [form="♀ (female)"]
  keys = screw terminal, 4 pins
  Pad1 = Pad [width=30 height=30 connect=center]  # not connected
  PCA9685 = female pin header, 6 pins [form="♀ (female)"]
  J5 = female pin header, 4 pins [form="♀ (female)"]  # not connected
  J6 = female pin header, 4 pins [form="♀ (female)"]  # not connected
  J7 = female pin header, 4 pins [form="♀ (female)"]  # not connected
  Pad2 = Pad [width=30 height=30 connect=center]  # not connected
  J8 = female pin header, 4 pins [form="♀ (female)"]  # not connected
  J9 = female pin header, 4 pins [form="♀ (female)"]  # not connected
  J10 = female pin header, 4 pins [form="♀ (female)"]  # not connected
  J11 = female pin header, 4 pins [form="♀ (female)"]  # not connected
  J12 = female pin header, 4 pins [form="♀ (female)"]  # not connected
  J13 = female pin header, 4 pins [form="♀ (female)"]  # not connected
  J14 = female pin header, 4 pins [form="♀ (female)"]  # not connected
  J15 = female pin header, 4 pins [form="♀ (female)"]  # not connected
  J16 = female pin header, 4 pins [form="♀ (female)"]
  U1 = Voltage Regulator - 5V [package="TO220 [THT]"]
  C1 = Electrolytic Capacitor [capacitance=47µF package="100 mil [THT, electrolytic]"]
  C2 = Ceramic Capacitor [capacitance=220nF package="100 mil [THT, multilayer]"]
  C3 = Ceramic Capacitor [capacitance=220nF package="100 mil [THT, multilayer]"]
  OUT+ = female pin header, 1 pin [form="♀ (female)"]
  OUT- = female pin header, 1 pin [form="♀ (female)"]
  OUT+_2 = female pin header, 1 pin [form="♀ (female)"]
  OUT-_2 = female pin header, 1 pin [form="♀ (female)"]
  IC1 = IC, DIP package, 4 pins [chip_label=IC]
  R1 = Resistor [tolerance=±5% resistance=470 package=THT]
  USB_5V+ = female pin header, 1 pin [form="♀ (female)"]
  J20 = female pin header, 1 pin [form="♀ (female)"]  # not connected
  J21 = female pin header, 1 pin [form="♀ (female)"]  # not connected
  USB_GND = female pin header, 1 pin [form="♀ (female)"]
  R2 = Resistor [tolerance=±5% resistance=1k package=THT]
  LED0_PWM = female pin header, 1 pin [form="♀ (female)"]
  LED0_IN+ = female pin header, 1 pin [form="♀ (female)"]
  LED0_IN- = female pin header, 1 pin [form="♀ (female)"]
  LED1_PWM = female pin header, 1 pin [form="♀ (female)"]
  LED1_IN+ = female pin header, 1 pin [form="♀ (female)"]
  LED1_IN- = female pin header, 1 pin [form="♀ (female)"]
  5V = female pin header, 2 pins [form="♀ (female)"]
  12V+_in = screw terminal, 2 pins
  5V+ = screw terminal, 2 pins
  LED_0 = screw terminal, 2 pins
  LED_1 = screw terminal, 2 pins
  5V_switched = screw terminal, 2 pins
  U2 = Voltage Regulator - 5V [package="TO220 [THT]"]
  Part2 = NRF24L01+ Breakout Board  # not connected
  C2_2 = Electrolytic Capacitor [capacitance=1µF package="100 mil [THT, electrolytic]"]

nets:
  N1: Raspberry_P1.pin1, Raspberry_P1.pin2, U1.output_voltage, 5V+.pin2, C2_2.+
  N2: Raspberry_P1.pin7, keys.pin1, C2.0
  N3: Raspberry_P1.pin8, R1.Pin_1
  N4: Raspberry_P1.pin9, keys.pin2, C2.1
  N5: Raspberry_P1.pin10, keys.pin3, C3.1
  N6: Raspberry_P1.pin11, keys.pin4, C3.0
  N7: Raspberry_P1.pin18, PCA9685.pin5, R2.Pin_1
  GND: Raspberry_P1.pin21, PCA9685.pin6, U1.GND, C1.-, IC1.pin2, USB_GND.pin1, LED0_IN-.pin1, LED1_IN-.pin1, 5V.pin1, 12V+_in.pin1, 5V+.pin1, 5V_switched.pin1, U2.GND, C2_2.-
  N8: Raspberry_P1.pin38, PCA9685.pin4
  N9: Raspberry_P1.pin39, PCA9685.pin3
  N10: Raspberry_P1.pin40, R2.Pin_0
  N11: PCA9685.pin1, PCA9685.pin2, C1.+, IC1.pin4, 5V.pin2, U2.output_voltage
  N12: J16.pin3, LED1_PWM.pin1
  N13: J16.pin4, LED0_PWM.pin1
  N14: U1.input_voltage, LED0_IN+.pin1, LED1_IN+.pin1, 12V+_in.pin2, U2.input_voltage
  N15: OUT+.pin1, LED_1.pin2
  N16: OUT-.pin1, LED_1.pin1
  N17: OUT+_2.pin1, LED_0.pin2
  N18: OUT-_2.pin1, LED_0.pin1
  N19: IC1.pin1, R1.Pin_0
  N20: IC1.pin3, USB_5V+.pin1, 5V_switched.pin2

notes:
  5V+
  AlarmPi
  LED1 driver
  LED0 driver
  USB 5V out sound
  Raspberry
  12V Supply
  gpio23
  GND
  gpio24
  gpio25
  gpio16
  3,3V
  IIC SDA
  IIC SCL
  SPI MOSI
  SPI SCLK
  Alarm Pi
  key 1
  key 2
